# Fritzing sketch Wiring (saved by Fritzing 0.9.3b)
breadboards: 1

parts:
  Raspberry_Pi1 = Raspberry Pi 2
  Part1 = ITEAD PN532 NFC Module
  Stop = Pushbutton [package="[SMD]"]
  Start = Pushbutton [package="[SMD]"]

nets:
  GND: Raspberry_Pi1.GND, Part1.GND, Start.Pin_1, Start.Pin_2
  N1: Raspberry_Pi1.GIPO26, Stop.Pin_3, Stop.Pin_4
  N2: Raspberry_Pi1.GIPO16, Start.Pin_3, Start.Pin_4
  N3: Raspberry_Pi1.GIPO25, Part1.SCK#12
  N4: Raspberry_Pi1.GIPO24, Part1.MI
  N5: Raspberry_Pi1.GIPO23, Part1.MO/SDA/TX
  N6: Raspberry_Pi1.GIPO18, Part1.NSS/SCL/RX, Part1.SCK#49
  5V: Raspberry_Pi1.5V, Part1.5V, Part1.3.3V, Stop.Pin_1, Stop.Pin_2

custom parts:
  ITEAD PN532 NFC Module: Breakout board Platform Based On Arduino by Iteadstudio Principal features : Electronic Brick Ports 3.3V or 5V power supply The official support forum: support@iteadstudio.com
